# Fritzing sketch BlueHammer_PiezoSensor (saved by Fritzing 0.9.2b)
breadboards: 1

parts:
  Bauteil1 = Arduino Mega ADK (Rev3)
  R1 = Resistor [tolerance=±5% resistance=220 package=THT]
  J1 = Piezo Speaker

nets:
  N1: Bauteil1.A0, R1.Pin_1, J1.pin2
  N2: Bauteil1.GND, R1.Pin_0, J1.pin1
