# Fritzing sketch EisbaerCircuits (saved by Fritzing 0.9.2b)
breadboards: 1

parts:
  Bauteil1 = Arduino Mega 2560 (Rev3)
  R1 = Resistor [tolerance=±5% resistance=220 package=THT]
  R2 = Resistor [tolerance=±5% resistance=220 package=THT]
  R3 = Resistor [tolerance=±5% resistance=220 package=THT]
  R4 = Resistor [tolerance=±5% resistance=220 package=THT]
  R5 = Resistor [tolerance=±5% resistance=220 package=THT]
  R6 = Resistor [tolerance=±5% resistance=220 package=THT]
  LED1 = LED - 5mm [color="Yellow (595nm)" package="5 mm [THT]"]
  LED2 = LED - 5mm [color="Yellow (595nm)" package="5 mm [THT]"]
  LED3 = LED - 5mm [color="Yellow (595nm)" package="5 mm [THT]"]
  LED4 = LED - 5mm [color="Yellow (595nm)" package="5 mm [THT]"]
  LED5 = LED - 5mm [color="Yellow (595nm)" package="5 mm [THT]"]
  LED6 = LED - 5mm [color="Yellow (595nm)" package="5 mm [THT]"]
  LED7 = LED - 5mm [color="Yellow (595nm)" package="5 mm [THT]"]
  LED8 = LED - 5mm [color="Yellow (595nm)" package="5 mm [THT]"]
  LED9 = LED - 5mm [color="Yellow (595nm)" package="5 mm [THT]"]
  LED10 = LED - 5mm [color="Yellow (595nm)" package="5 mm [THT]"]
  LED11 = LED - 5mm [color="Yellow (595nm)" package="5 mm [THT]"]
  LED12 = LED - 5mm [color="Yellow (595nm)" package="5 mm [THT]"]
  LED13 = LED - 5mm [color="Yellow (595nm)" package="5 mm [THT]"]
  LED14 = LED - 5mm [color="Yellow (595nm)" package="5 mm [THT]"]
  LED16 = LED - 5mm [color="Yellow (595nm)" package="5 mm [THT]"]
  LED17 = LED - 5mm [color="Yellow (595nm)" package="5 mm [THT]"]
  LED18 = LED - 5mm [color="Yellow (595nm)" package="5 mm [THT]"]
  LED19 = LED - 5mm [color="Yellow (595nm)" package="5 mm [THT]"]
  LED21 = LED - 5mm [color="Yellow (595nm)" package="5 mm [THT]"]
  LED22 = LED - 5mm [color="Yellow (595nm)" package="5 mm [THT]"]
  LED23 = LED - 5mm [color="Yellow (595nm)" package="5 mm [THT]"]
  LED24 = LED - 5mm [color="Yellow (595nm)" package="5 mm [THT]"]
  LED25 = LED - 5mm [color="Yellow (595nm)" package="5 mm [THT]"]
  LED26 = LED - 5mm [color="Yellow (595nm)" package="5 mm [THT]"]
  LED27 = LED - 5mm [color="Yellow (595nm)" package="5 mm [THT]"]
  LED28 = LED - 5mm [color="Yellow (595nm)" package="5 mm [THT]"]
  LED29 = LED - 5mm [color="Yellow (595nm)" package="5 mm [THT]"]
  LED30 = LED - 5mm [color="Yellow (595nm)" package="5 mm [THT]"]
  LED31 = LED - 5mm [color="Yellow (595nm)" package="5 mm [THT]"]
  LED32 = LED - 5mm [color="Yellow (595nm)" package="5 mm [THT]"]
  LED33 = LED - 5mm [color="Yellow (595nm)" package="5 mm [THT]"]
  LED34 = LED - 5mm [color="Yellow (595nm)" package="5 mm [THT]"]
  LED35 = RGB LED (com. cathode, rgb) [package="5 mm [THT]"]
  Q1 = NPN-Transistor [package="TO92 [THT]"]
  Q2 = NPN-Transistor [package="TO92 [THT]"]
  Q3 = NPN-Transistor [package="TO92 [THT]"]
  Q4 = NPN-Transistor [package="TO92 [THT]"]
  Q5 = NPN-Transistor [package="TO92 [THT]"]
  Q6 = NPN-Transistor [package="TO92 [THT]"]
  Speaker = Piezo Speaker
  Lilypad_Vibe1 = Lilypad Vibe Motor
  Hammer = Crystal [frequency="16 Mhz" package=SMD]

nets:
  N1: Bauteil1.A0, Lilypad_Vibe1.Supply
  N2: Bauteil1.A1, Speaker.pin2
  N3: Bauteil1.A2, Hammer.pin_0
  GND: Bauteil1.GND, LED35.common_cathode, Q1.E, Q2.E, Q3.E, Q4.E, Q5.E, Q6.E, Speaker.pin1, Lilypad_Vibe1.GND, Hammer.pin_1
  N4: Bauteil1.D2_PWM, R2.Pin_0
  N5: Bauteil1.D3_PWM, R1.Pin_0
  N6: Bauteil1.D4_PWM, R3.Pin_0
  N7: Bauteil1.D5_PWM, R4.Pin_0
  N8: Bauteil1.D6_PWM, R5.Pin_0
  N9: Bauteil1.D7_PWM, R6.Pin_0
  N10: Bauteil1.D23, Q1.B
  N11: Bauteil1.D24, Q2.B
  N12: Bauteil1.D25, Q3.B
  N13: Bauteil1.D26, Q4.B
  N14: Bauteil1.D27, Q5.B
  N15: Bauteil1.D28, Q6.B
  N16: Bauteil1.D43, LED35.red_anode
  N17: Bauteil1.D44, LED35.blue_anode
  N18: Bauteil1.D45, LED35.green_anode
  N19: R1.Pin_1, LED29.anode, LED30.anode, LED31.anode, LED32.anode, LED33.anode, LED34.anode
  N20: R2.Pin_1, LED23.anode, LED24.anode, LED25.anode, LED26.anode, LED27.anode, LED28.anode
  N21: R3.Pin_1, LED18.anode, LED19.anode, LED21.anode, LED22.anode
  N22: R4.Pin_1, LED13.anode, LED14.anode, LED16.anode, LED17.anode
  N23: R5.Pin_1, LED7.anode, LED9.anode, LED10.anode, LED11.anode, LED12.anode
  N24: R6.Pin_1, LED1.anode, LED2.anode, LED3.anode, LED4.anode, LED5.anode, LED6.anode
  N25: LED1.cathode, LED8.cathode, LED14.cathode, LED19.cathode, LED24.cathode, LED30.cathode, Q1.C
  N26: LED2.cathode, LED7.cathode, LED13.cathode, LED18.cathode, LED23.cathode, LED29.cathode, Q2.C
  N27: LED3.cathode, LED12.cathode, LED28.cathode, LED34.cathode, Q3.C
  N28: LED4.cathode, LED11.cathode, LED17.cathode, LED22.cathode, LED27.cathode, LED33.cathode, Q6.C
  N29: LED5.cathode, LED10.cathode, LED16.cathode, LED21.cathode, LED26.cathode, LED32.cathode, Q5.C
  N30: LED6.cathode, LED9.cathode, LED25.cathode, LED31.cathode, Q4.C
