# Fritzing sketch EisbaerCircuitsv2 (saved by Fritzing 0.9.2b)
breadboards: 1

parts:
  Bauteil1 = Arduino Mega 2560 (Rev3)
  LED2 = LED - 5mm [color="Yellow (595nm)" package="5 mm [THT]"]
  LED3 = LED - 5mm [color="Yellow (595nm)" package="5 mm [THT]"]
  LED4 = LED - 5mm [color="Yellow (595nm)" package="5 mm [THT]"]
  LED5 = LED - 5mm [color="Yellow (595nm)" package="5 mm [THT]"]
  LED6 = LED - 5mm [color="Yellow (595nm)" package="5 mm [THT]"]
  LED7 = LED - 5mm [color="Yellow (595nm)" package="5 mm [THT]"]
  LED8 = LED - 5mm [color="Yellow (595nm)" package="5 mm [THT]"]
  LED9 = LED - 5mm [color="Yellow (595nm)" package="5 mm [THT]"]
  LED10 = LED - 5mm [color="Yellow (595nm)" package="5 mm [THT]"]
  LED11 = LED - 5mm [color="Yellow (595nm)" package="5 mm [THT]"]
  LED12 = LED - 5mm [color="Yellow (595nm)" package="5 mm [THT]"]
  LED13 = LED - 5mm [color="Yellow (595nm)" package="5 mm [THT]"]
  LED14 = LED - 5mm [color="Yellow (595nm)" package="5 mm [THT]"]
  LED16 = LED - 5mm [color="Yellow (595nm)" package="5 mm [THT]"]
  LED17 = LED - 5mm [color="Yellow (595nm)" package="5 mm [THT]"]
  LED18 = LED - 5mm [color="Yellow (595nm)" package="5 mm [THT]"]
  LED19 = LED - 5mm [color="Yellow (595nm)" package="5 mm [THT]"]
  LED21 = LED - 5mm [color="Yellow (595nm)" package="5 mm [THT]"]
  LED22 = LED - 5mm [color="Yellow (595nm)" package="5 mm [THT]"]
  LED23 = LED - 5mm [color="Yellow (595nm)" package="5 mm [THT]"]
  LED24 = LED - 5mm [color="Yellow (595nm)" package="5 mm [THT]"]
  LED25 = LED - 5mm [color="Yellow (595nm)" package="5 mm [THT]"]
  LED26 = LED - 5mm [color="Yellow (595nm)" package="5 mm [THT]"]
  LED27 = LED - 5mm [color="Yellow (595nm)" package="5 mm [THT]"]
  LED28 = LED - 5mm [color="Yellow (595nm)" package="5 mm [THT]"]
  LED29 = LED - 5mm [color="Yellow (595nm)" package="5 mm [THT]"]
  LED30 = LED - 5mm [color="Yellow (595nm)" package="5 mm [THT]"]
  LED31 = LED - 5mm [color="Yellow (595nm)" package="5 mm [THT]"]
  LED32 = LED - 5mm [color="Yellow (595nm)" package="5 mm [THT]"]
  LED33 = LED - 5mm [color="Yellow (595nm)" package="5 mm [THT]"]
  LED34 = LED - 5mm [color="Yellow (595nm)" package="5 mm [THT]"]
  Q1 = NPN-Transistor [package="TO92 [THT]"]
  Q2 = NPN-Transistor [package="TO92 [THT]"]
  Q3 = NPN-Transistor [package="TO92 [THT]"]
  Q4 = NPN-Transistor [package="TO92 [THT]"]
  Q5 = NPN-Transistor [package="TO92 [THT]"]
  Q6 = NPN-Transistor [package="TO92 [THT]"]
  Lilypad_Vibe1 = Lilypad Vibe Motor
  LED36 = RGB LED (6 legs) [package="5 mm [THT]"]
  0_0 = LED - 5mm [color="Green (570nm)" part_number=LED0,0 package="5 mm [THT]"]
  J1 = Basic Force Sensing Resistor (FSR) [package=THT]  # not connected
  J2 = Piezo Speaker  # not connected

nets:
  GND: Bauteil1.GND, Q1.E, Q2.E, Q3.E, Q4.E, Q5.E, Q6.E, Lilypad_Vibe1.GND, LED36.GND
  N1: Bauteil1.D2_PWM, LED2.anode, LED3.anode, LED4.anode, LED5.anode, LED6.anode, 0_0.anode
  N2: Bauteil1.D3_PWM, LED7.anode, LED8.anode, LED9.anode, LED10.anode, LED11.anode, LED12.anode
  N3: Bauteil1.D4_PWM, LED13.anode, LED14.anode, LED16.anode, LED17.anode
  N4: Bauteil1.D5_PWM, LED18.anode, LED19.anode, LED21.anode, LED22.anode
  N5: Bauteil1.D6_PWM, LED23.anode, LED24.anode, LED25.anode, LED26.anode, LED27.anode, LED28.anode
  N6: Bauteil1.D7_PWM, LED29.anode, LED30.anode, LED31.anode, LED32.anode, LED33.anode, LED34.anode
  N7: Bauteil1.D22, Q1.B
  N8: Bauteil1.D24, Q2.B
  N9: Bauteil1.D26, Q3.B
  N10: Bauteil1.D28, Q4.B
  N11: Bauteil1.D30, Q5.B
  N12: Bauteil1.D32, Q6.B
  N13: Bauteil1.D42, LED36.Red
  N14: Bauteil1.D44, LED36.Blue1
  N15: Bauteil1.D46, LED36.Blue2
  N16: Bauteil1.D48, LED36.Green
  N17: Bauteil1.D52, Lilypad_Vibe1.Supply
  N18: LED2.cathode, LED7.cathode, LED13.cathode, LED18.cathode, LED23.cathode, LED29.cathode, Q2.C
  N19: LED3.cathode, LED12.cathode, LED28.cathode, LED34.cathode, Q3.C
  N20: LED4.cathode, LED11.cathode, LED17.cathode, LED22.cathode, LED27.cathode, LED33.cathode, Q6.C
  N21: LED5.cathode, LED10.cathode, LED16.cathode, LED21.cathode, LED26.cathode, LED32.cathode, Q5.C
  N22: LED6.cathode, LED9.cathode, LED25.cathode, LED31.cathode, Q4.C
  N23: LED8.cathode, LED14.cathode, LED19.cathode, LED24.cathode, LED30.cathode, Q1.C, 0_0.cathode

notes:
  (0|0)
  (0|1)
  (1|0)
  (5|5)
  pinkHammer
  blueHammer
