# Fritzing sketch PinkHammer_TouchSensor (saved by Fritzing 0.9.2b)
breadboards: 1

parts:
  Bauteil1 = Arduino Mega ADK (Rev3)
  J1 = Basic Force Sensing Resistor (FSR) [package=THT]
  R1 = Resistor [tolerance=±5% resistance=220 package=THT]

nets:
  N1: Bauteil1.A2, J1.pin_0, R1.Pin_1
  N2: Bauteil1.5V, J1.pin_1
  N3: Bauteil1.GND, R1.Pin_0
